# Fritzing sketch demo_sketch (saved by Fritzing 0.8.3b)
breadboards: 1

parts:
  R4 = Resistor [tolerance=±5% resistance=1k package=THT]
  LED3 = LED - 5mm [color="Green (570nm)" package="5 mm [THT]"]
  R2 = Resistor [tolerance=±5% resistance=330 package=THT]
  S2 = Pushbutton [package="[THT]"]
  R3 = Resistor [tolerance=±5% resistance=330 package=THT]
  R1 = Resistor [tolerance=±5% resistance=330 package=THT]
  LED1 = LED - 5mm [color="Red (633nm)" package="5 mm [THT]"]
  LED2 = LED - 5mm [color="Yellow (595nm)" package="5 mm [THT]"]
  BeagleBone1 = BeagleBone Black

nets:
  N1: R4.Pin_0, S2.Pin_1, S2.Pin_2, BeagleBone1.no_name_yet#116
  GND: R4.Pin_1, LED3.cathode, LED1.cathode, LED2.cathode, BeagleBone1.no_name_yet#102
  N2: LED3.anode, R3.Pin_1
  N3: R2.Pin_0, BeagleBone1.no_name_yet#113
  N4: R2.Pin_1, LED2.anode
  3.3V: S2.Pin_3, S2.Pin_4, BeagleBone1.no_name_yet#3
  N5: R3.Pin_0, BeagleBone1.no_name_yet#115
  N6: R1.Pin_0, BeagleBone1.no_name_yet#112
  N7: R1.Pin_1, LED1.anode

custom parts:
  BeagleBone Black: BeagleBone Black rev. A5B
